# Fritzing sketch FritzingDiagram_CA2 (saved by Fritzing 0.9.3b)
breadboards: 1

parts:
  Part1 = Adafruit T-Cobbler Plus [part_number="Adafruit #1989 and #2028"]
  ADC1 = MCP3008 [package=dil16]
  LED2 = smd LED [color="Red (633nm)" package="0603 [SMD]"]
  R3 = Resistor [tolerance=±5% resistance=330 package="2010 [SMD]"]
  R4 = Photocell (LDR) [package=THT]
  R5 = Resistor [tolerance=±5% resistance=10k package="2010 [SMD]"]
  DHT2 = DHT11 Humitidy and Temperature Sensor
  R6 = Resistor [tolerance=±5% resistance=10k package="2010 [SMD]"]

nets:
  VDD: Part1.+3.3V, ADC1.VREF, ADC1.VDD, R5.Pin_0, DHT2.VDD, R6.Pin_0
  N1: Part1.GPIO4, DHT2.DATA, R6.Pin_1
  GND: Part1.GND, DHT2.GND
  N2: Part1.MOSI, ADC1.Din
  N3: Part1.MISO, ADC1.Dout
  N4: Part1.SCLK, ADC1.CLK
  N5: Part1.GPIO18, LED2.anode
  N6: Part1.CE0, ADC1.CS/SHDN
  N7: ADC1.CH0, R4.pin_0, R5.Pin_1
  N8: ADC1.DGND, ADC1.AGND, R3.Pin_0, R4.pin_1
  N9: LED2.cathode, R3.Pin_1

custom parts:
  Adafruit T-Cobbler Plus: The Raspberry Pi has landed on the Maker World like a 40-GPIO pinned, quad-USB ported, credit card sized bomb of DIY joy. And while you can use most of our great Model B accessories by hooking up our downgrade cable, its probably a good time to upgrade your set up and accessorize using all of the 40 pins. That's why we now carry the Assembled Adafruit Pi T-Cobbler Plus - Breakout + Cable for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
  DHT11 Humitidy and Temperature Sensor: DHT11 Humidity and Temperature Sensor
